# Fritzing sketch RS-555-BlackBox (saved by Fritzing 0.9.3b)
breadboards: 1

parts:
  U1 = 555 Timer [package="DIP8 [THT]"]
  C1 = Ceramic Capacitor [capacitance=1nF voltage=6.3V package="100 mil [THT, multilayer]"]
  R2 = Resistor [tolerance=±5% resistance=1k package=THT]
  R1 = Resistor [tolerance=±5% resistance=10k package=THT]
  R3 = Resistor [tolerance=±5% resistance=100 package=THT]
  SP1 = SPEAKER [package=pcb_mount_speaker]

nets:
  GND: U1.Ground, C1.0
  N1: U1.Trigger, U1.Threshold, C1.1, R2.Pin_0
  N2: U1.Output, R3.Pin_1
  6V: U1.Reset, U1.Vcc_Supply_Voltage, R1.Pin_1, SP1.+
  N3: U1.Discharge, R2.Pin_1, R1.Pin_0
  N4: R3.Pin_0, SP1.-

notes:
  Speaker on the Lab board.
  To board Ground
  To board Vcc
